# Fritzing sketch nodemcuv1_ds18b20 (saved by Fritzing 0.9.3b)
breadboards: 1

parts:
  DS1 = DS18B20 1-Wire Temperature Sensor [part_number=DS18B20]
  R1 = Resistor [tolerance=±5% resistance=4.7k package=THT]
  U1 = NodeMCU V1.0

nets:
  N1: DS1.DQ, R1.Pin_1, U1.D3
  N2: DS1.VDD, R1.Pin_0

custom parts:
  NodeMCU V1.0: ESP8266 based NodeMCU
